// Logisim project labo_cheni_corrige_decompteur.circ as structural Verilog: 5 circuits, main circuit MAXV_CHENILLARD
module MAXV_CHENILLARD (
  input  [7:0] switch_i,
  input  clk_i,
  input  nReset_i,
  output [7:0] led_o
);

  wire entree_i_sw6, entree_i_sw7, entree_i_sw8, not_1_out;
  wire [1:0] entree_i_sw2;

  DipSwitch entree_i (
    .sw1(entree_i_sw2[1]), .sw2(entree_i_sw2[0]), .sw6(entree_i_sw6), .sw7(entree_i_sw7), .sw8(entree_i_sw8));  // open: sw3, sw4, sw5
  not not_1 (not_1_out, nReset_i);
  chenillard_TOP chenillard_top_1 (
    .val_i(switch_i), .load_i(entree_i_sw7), .right_nleft_i(entree_i_sw6), .enable_i(entree_i_sw8),
    .speed_i(entree_i_sw2), .clk_i(clk_i), .reset_i(not_1_out), .led_o(led_o));

  // Notes on the sheet:
  //   Attention, votre version de Logisim
  //   ne contient pas de tracker. Si vous
  //   enregistrez votre projet, toutes les
  //   informations du tracker seront
  //   définitivement effacées.
endmodule

module chenillard_TOP (
  input  [7:0] val_i,
  input  load_i,
  input  right_nleft_i,
  input  enable_i,
  input  [1:0] speed_i,
  input  clk_i,
  input  reset_i,
  output [7:0] led_o
);

  wire and_1_out, timer_28b_1_done_o;
  wire [1:0] or_1_out;
  wire [27:0] multiplexer_1_out;

  Multiplexer #(.select(2), .width(28), .enable("false")) multiplexer_1 (
    .in0(28'h2), .in1(28'he4e1bf), .in2(28'h1c9c37f), .in3(28'h39386ff), .out(multiplexer_1_out),
    .sel(speed_i));
  and and_1 (and_1_out, right_nleft_i, timer_28b_1_done_o, enable_i);
  or or_1 (or_1_out[0], load_i, and_1_out);
  and and_2 (or_1_out[1], ~load_i, enable_i, timer_28b_1_done_o);  // AND_Gate
  timer_28b timer_28b_1 (
    .value_i(multiplexer_1_out), .load_i(load_i), .en_i(enable_i), .clk_i(clk_i), .reset_i(reset_i),
    .done_o(timer_28b_1_done_o));
  shift_reg_8b shift_reg_8b_1 (
    .ser_r_i(led_o[0]), .ser_l_i(led_o[7]), .value_load_i(val_i), .mode_i(or_1_out), .clk_i(clk_i),
    .reset_i(reset_i), .val_o(led_o));

  // Notes on the sheet:
  //   Attention, votre version de Logisim
  //   ne contient pas de tracker. Si vous
  //   enregistrez votre projet, toutes les
  //   informations du tracker seront
  //   définitivement effacées.
endmodule

module shift_reg_4b (
  input  ser_r_i,
  input  ser_l_i,
  input  [3:0] value_load_i,
  input  [1:0] mode_i,
  input  clk_i,
  input  reset_i,
  output [3:0] val_o
);

  wire multiplexer_1_out, multiplexer_2_out, multiplexer_3_out, multiplexer_4_out;

  Multiplexer #(.select(2), .enable("false")) multiplexer_1 (
    .in0(val_o[0]), .in1(value_load_i[0]), .in2(ser_l_i), .in3(val_o[1]), .out(multiplexer_1_out),
    .sel(mode_i));
  D_Flip_Flop d_ff_1 (.D(multiplexer_1_out), .clk(clk_i), .Q(val_o[0]), .preset(1'b0), .reset(reset_i));  // open: Qn
  Multiplexer #(.select(2), .enable("false")) multiplexer_2 (
    .in0(val_o[1]), .in1(value_load_i[1]), .in2(val_o[0]), .in3(val_o[2]), .out(multiplexer_2_out),
    .sel(mode_i));
  D_Flip_Flop d_ff_2 (.D(multiplexer_2_out), .clk(clk_i), .Q(val_o[1]), .preset(1'b0), .reset(reset_i));  // open: Qn
  Multiplexer #(.select(2), .enable("false")) multiplexer_3 (
    .in0(val_o[2]), .in1(value_load_i[2]), .in2(val_o[1]), .in3(val_o[3]), .out(multiplexer_3_out),
    .sel(mode_i));
  D_Flip_Flop d_ff_3 (.D(multiplexer_3_out), .clk(clk_i), .Q(val_o[2]), .preset(1'b0), .reset(reset_i));  // open: Qn
  Multiplexer #(.select(2), .enable("false")) multiplexer_4 (
    .in0(val_o[3]), .in1(value_load_i[3]), .in2(val_o[2]), .in3(ser_r_i), .out(multiplexer_4_out),
    .sel(mode_i));
  D_Flip_Flop d_ff_4 (.D(multiplexer_4_out), .clk(clk_i), .Q(val_o[3]), .preset(1'b0), .reset(reset_i));  // open: Qn

  // Notes on the sheet:
  //   Attention, votre version de Logisim
  //   ne contient pas de tracker. Si vous
  //   enregistrez votre projet, toutes les
  //   informations du tracker seront
  //   définitivement effacées.
endmodule

module shift_reg_8b (
  input  ser_r_i,
  input  ser_l_i,
  input  [7:0] value_load_i,
  input  [1:0] mode_i,
  input  clk_i,
  input  reset_i,
  output [7:0] val_o
);

  shift_reg_4b shift_reg_4b_1 (
    .ser_r_i(val_o[4]), .ser_l_i(ser_l_i), .value_load_i(value_load_i[3:0]), .mode_i(mode_i), .clk_i(clk_i),
    .reset_i(reset_i), .val_o(val_o[3:0]));
  shift_reg_4b shift_reg_4b_2 (
    .ser_r_i(ser_r_i), .ser_l_i(val_o[3]), .value_load_i(value_load_i[7:4]), .mode_i(mode_i), .clk_i(clk_i),
    .reset_i(reset_i), .val_o(val_o[7:4]));

  // Notes on the sheet:
  //   Attention, votre version de Logisim
  //   ne contient pas de tracker. Si vous
  //   enregistrez votre projet, toutes les
  //   informations du tracker seront
  //   définitivement effacées.
endmodule

module timer_28b (
  input  [27:0] value_i,
  input  load_i,
  input  en_i,
  input  clk_i,
  input  reset_i,
  output done_o
);

  wire or_1_out;
  wire [27:0] multiplexer_1_out, multiplexer_2_out, register_1_q, subtractor_1_out;

  or or_1 (or_1_out, load_i, done_o);
  Multiplexer #(.width(28), .enable("false")) multiplexer_1 (
    .in0(subtractor_1_out), .in1(value_i), .out(multiplexer_1_out), .sel(or_1_out));
  Register #(.width(28)) register_1 (.D(multiplexer_2_out), .en(1'b1), .clk(clk_i), .Q(register_1_q), .clr(reset_i));
  Multiplexer #(.width(28), .enable("false")) multiplexer_2 (
    .in0(value_i), .in1(multiplexer_1_out), .out(multiplexer_2_out), .sel(en_i));
  Subtractor #(.width(28)) subtractor_1 (
    .a(register_1_q), .b(28'h1), .out(subtractor_1_out), .bin(1'b0));  // open: bout
  Comparator #(.width(28), .mode("unsigned")) comparator_1 (
    .a(register_1_q), .b({28{1'b0}}), .eq(done_o));  // open: gt, lt

  // Notes on the sheet:
  //   Attention, votre version de Logisim
  //   ne contient pas de tracker. Si vous
  //   enregistrez votre projet, toutes les
  //   informations du tracker seront
  //   définitivement effacées.
endmodule
