// Logisim project labo1.circ as structural Verilog: 3 circuits, main circuit main
module main (
);


  // Notes on the sheet:
  //   Attention, votre version de Logisim
  //   ne contient pas de tracker. Si vous
  //   enregistrez votre projet, toutes les
  //   informations du tracker seront
  //   définitivement effacées.
endmodule

module Add1bit (
  input  A,
  input  B,
  input  C_in,
  output D,
  output C_out
);

  wire and_1_out, and_2_out, and_3_out, xor_1_out;

  and and_1 (and_1_out, A, B);
  and and_2 (and_2_out, A, C_in);
  and and_3 (and_3_out, B, C_in);
  xor xor_1 (xor_1_out, A, B);
  xor xor_2 (D, xor_1_out, C_in);
  or or_1 (C_out, and_1_out, and_2_out, and_3_out);

  // Notes on the sheet:
  //   Attention, votre version de Logisim
  //   ne contient pas de tracker. Si vous
  //   enregistrez votre projet, toutes les
  //   informations du tracker seront
  //   définitivement effacées.
endmodule

module Add4bits (
  input  C_in,
  input  [3:0] A,
  input  [3:0] B,
  input  [3:0] in_4,
  input  C_out
);

  wire AddBit_0_c_out, AddBit_1_c_out, AddBit_2_c_out;

  Add1bit AddBit_0 (.A(A[0]), .B(B[0]), .C_in(C_in), .D(in_4[0]), .C_out(AddBit_0_c_out));
  Add1bit AddBit_1 (.A(A[1]), .B(B[1]), .C_in(AddBit_0_c_out), .D(in_4[1]), .C_out(AddBit_1_c_out));
  Add1bit AddBit_2 (.A(A[2]), .B(B[2]), .C_in(AddBit_1_c_out), .D(in_4[2]), .C_out(AddBit_2_c_out));
  Add1bit AddBit_3 (.A(A[3]), .B(B[3]), .C_in(AddBit_2_c_out), .D(in_4[3]), .C_out(C_out));

  // Notes on the sheet:
  //   Attention, votre version de Logisim
  //   ne contient pas de tracker. Si vous
  //   enregistrez votre projet, toutes les
  //   informations du tracker seront
  //   définitivement effacées.
endmodule
