// Logisim project labo_alu_etu.circ as structural Verilog: 9 circuits, main circuit ALU_MAXV
module ALU_MAXV (
  input  [3:0] a_i,
  input  [3:0] b_i,
  output [3:0] c_o,
  output erreur_o
);

  wire [5:0] opcode_i_sw6;

  DipSwitch opcode_i (
    .sw1(opcode_i_sw6[5]), .sw2(opcode_i_sw6[4]), .sw3(opcode_i_sw6[3]), .sw4(opcode_i_sw6[2]),
    .sw5(opcode_i_sw6[1]), .sw6(opcode_i_sw6[0]));  // open: sw7, sw8
  ALU_Top alu_inst (.a_i(a_i), .b_i(b_i), .op_i(opcode_i_sw6), .c_o(c_o), .erreur_o(erreur_o));

  // Notes on the sheet:
  //   Attention, votre version de Logisim
  //   ne contient pas de tracker. Si vous
  //   enregistrez votre projet, toutes les
  //   informations du tracker seront
  //   définitivement effacées.
endmodule

module ALU_Top (
  input  [3:0] a_i,
  input  [3:0] b_i,
  input  [5:0] op_i,
  output [3:0] c_o,
  output erreur_o
);

  wire add_subb4bit_1_overflow, c, n, z;
  wire [3:0] add_subb4bit_1_r_o, alu_comp_1_cmp, alu_cus_1_s, alu_log_1_f;

  ALU_CUS alu_cus_1 (.a(a_i), .s(alu_cus_1_s));
  add_subb4bit add_subb4bit_1 (
    .a_i(a_i), .b_i(b_i), .opcode(op_i[3:2]), .r_o(add_subb4bit_1_r_o), .carry_o(c),
    .overflow(add_subb4bit_1_overflow), .zero_o(z), .Negative_o(n));
  ALU_COMP alu_comp_1 (.Negative_i(n), .zero_i(z), .carry_o(c), .op_code(op_i[2:0]), .cmp(alu_comp_1_cmp));
  ALU_LOG alu_log_1 (.a(a_i), .b(b_i), .op_code(op_i[1:0]), .F(alu_log_1_f));
  Multiplexer #(.select(2), .width(4), .enable("false")) multiplexer_1 (
    .in0(add_subb4bit_1_r_o), .in1(alu_comp_1_cmp), .in2(alu_log_1_f), .in3(alu_cus_1_s), .out(c_o),
    .sel(op_i[5:4]));
  ALU_ERREUR alu_erreur_1 (
    .overflow(add_subb4bit_1_overflow), .op_end(op_i[3:0]), .op_start(op_i[5:4]), .erreur(erreur_o));

  // Notes on the sheet:
  //   Attention, votre version de Logisim
  //   ne contient pas de tracker. Si vous
  //   enregistrez votre projet, toutes les
  //   informations du tracker seront
  //   définitivement effacées.
endmodule

module add1bit (
  input  a_i,
  input  b_i,
  input  c_i,
  output r_o,
  output c_o
);

  wire and_1_out, and_2_out, and_3_out, xor_1_out;

  xor xor_1 (xor_1_out, a_i, b_i);
  and and_1 (and_1_out, a_i, b_i);
  and and_2 (and_2_out, a_i, c_i);
  and and_3 (and_3_out, b_i, c_i);
  xor xor_2 (r_o, xor_1_out, c_i);
  or or_1 (c_o, and_1_out, and_2_out, and_3_out);

  // Notes on the sheet:
  //   Attention, votre version de Logisim
  //   ne contient pas de tracker. Si vous
  //   enregistrez votre projet, toutes les
  //   informations du tracker seront
  //   définitivement effacées.
endmodule

module add4bit (
  input  c_i,
  input  [3:0] a_i,
  input  [3:0] b_i,
  output [3:0] r_o,
  output c_o
);

  wire c_out1, c_out2, c_out3;

  add1bit add1bit_1 (.a_i(a_i[0]), .b_i(b_i[0]), .c_i(c_i), .r_o(r_o[0]), .c_o(c_out1));
  add1bit add1bit_2 (.a_i(a_i[1]), .b_i(b_i[1]), .c_i(c_out1), .r_o(r_o[1]), .c_o(c_out2));
  add1bit add1bit_3 (.a_i(a_i[2]), .b_i(b_i[2]), .c_i(c_out2), .r_o(r_o[2]), .c_o(c_out3));
  add1bit add1bit_4 (.a_i(a_i[3]), .b_i(b_i[3]), .c_i(c_out3), .r_o(r_o[3]), .c_o(c_o));

  // Notes on the sheet:
  //   Attention, votre version de Logisim
  //   ne contient pas de tracker. Si vous
  //   enregistrez votre projet, toutes les
  //   informations du tracker seront
  //   définitivement effacées.
endmodule

module add_subb4bit (
  input  [3:0] a_i,
  input  [3:0] b_i,
  input  [1:0] opcode,
  output [3:0] r_o,
  output carry_o,
  output overflow,
  output zero_o,
  output Negative_o
);

  wire and_2_out, and_3_out, or_1_out, xor_2_out, xor_3_out;
  wire [3:0] xor_1_out;

  assign xor_1_out = b_i ^ {4{opcode[1]}};  // XOR_Gate xor_1, 4 bits wide
  xor xor_2 (xor_2_out, r_o[3], overflow);
  and and_1 (Negative_o, ~opcode[0], xor_2_out);  // AND_Gate
  add4bit add4bit_1 (.c_i(opcode[1]), .a_i(a_i), .b_i(xor_1_out), .r_o(r_o), .c_o(carry_o));
  nor nor_1 (zero_o, r_o[3], r_o[2], r_o[1], r_o[0]);
  xor xor_3 (xor_3_out, carry_o, opcode[1]);
  and and_2 (and_2_out, a_i[3], xor_1_out[3], ~r_o[3]);  // AND_Gate
  and and_3 (and_3_out, ~a_i[3], ~xor_1_out[3], r_o[3]);  // AND_Gate
  or or_1 (or_1_out, and_2_out, and_3_out);
  Multiplexer #(.enable("false")) multiplexer_1 (.in0(or_1_out), .in1(xor_3_out), .out(overflow), .sel(opcode[0]));

  // Notes on the sheet:
  //   Attention, votre version de Logisim
  //   ne contient pas de tracker. Si vous
  //   enregistrez votre projet, toutes les
  //   informations du tracker seront
  //   définitivement effacées.
endmodule

module ALU_COMP (
  input  Negative_i,
  input  zero_i,
  input  carry_o,
  input  [2:0] op_code,
  output [3:0] cmp
);

  wire not_1_out, not_2_out, not_3_out;

  not not_1 (not_1_out, zero_i);
  not not_2 (not_2_out, Negative_i);
  not not_3 (not_3_out, carry_o);
  Multiplexer #(.select(3), .enable("false")) multiplexer_1 (
    .in0(1'b0), .in1(not_2_out), .in2(Negative_i), .in3(not_1_out), .in4(zero_i), .in5(carry_o),
    .in6(not_3_out), .in7(1'b0), .out(cmp[0]), .sel(op_code));

  assign cmp[3:1] = 3'b000;

  // Notes on the sheet:
  //   Attention, votre version de Logisim
  //   ne contient pas de tracker. Si vous
  //   enregistrez votre projet, toutes les
  //   informations du tracker seront
  //   définitivement effacées.
endmodule

module ALU_LOG (
  input  [3:0] a,
  input  [3:0] b,
  input  [1:0] op_code,
  output [3:0] F
);

  wire [3:0] and_1_out, not_1_out, or_1_out, xor_1_out;

  assign and_1_out = a & b;  // AND_Gate and_1, 4 bits wide
  assign or_1_out = a | b;  // OR_Gate or_1, 4 bits wide
  assign xor_1_out = a ^ b;  // XOR_Gate xor_1, 4 bits wide
  assign not_1_out = ~and_1_out;  // NOT_Gate not_1, 4 bits wide
  Multiplexer #(.select(2), .width(4), .enable("false")) multiplexer_1 (
    .in0(and_1_out), .in1(or_1_out), .in2(not_1_out), .in3(xor_1_out), .out(F), .sel(op_code));

  // Notes on the sheet:
  //   Attention, votre version de Logisim
  //   ne contient pas de tracker. Si vous
  //   enregistrez votre projet, toutes les
  //   informations du tracker seront
  //   définitivement effacées.
endmodule

module ALU_CUS (
  input  [3:0] a,
  output [3:0] s
);

  wire and_1_out, and_2_out, and_3_out, and_4_out, or_1_out, or_2_out;

  and and_1 (and_1_out, a[0], ~a[1], ~a[2], ~a[3]);  // AND_Gate
  and and_2 (and_2_out, ~a[0], a[1], ~a[2], ~a[3]);  // AND_Gate
  and and_3 (and_3_out, ~a[0], ~a[1], a[2], ~a[3]);  // AND_Gate
  and and_4 (and_4_out, ~a[0], ~a[1], ~a[2], a[3]);  // AND_Gate
  or or_1 (or_1_out, and_1_out, and_2_out);
  or or_2 (or_2_out, and_3_out, and_4_out);
  or or_3 (s[0], or_1_out, or_2_out);

  assign s[3:1] = 3'b000;

  // Notes on the sheet:
  //   Attention, votre version de Logisim
  //   ne contient pas de tracker. Si vous
  //   enregistrez votre projet, toutes les
  //   informations du tracker seront
  //   définitivement effacées.
endmodule

module ALU_ERREUR (
  input  overflow,
  input  [3:0] op_end,
  input  [1:0] op_start,
  output erreur
);

  wire and_1_out, and_2_out, or_1_out;

  and and_1 (and_1_out, op_end[0], op_end[1], op_end[2]);
  and and_2 (and_2_out, ~op_end[0], ~op_end[1], ~op_end[2]);  // AND_Gate
  or or_1 (or_1_out, and_1_out, and_2_out, ~op_end[3]);  // OR_Gate
  Multiplexer #(.select(2), .enable("false")) multiplexer_1 (
    .in0(overflow), .in1(or_1_out), .in2(1'b0), .in3(1'b0), .out(erreur), .sel(op_start));

  // Notes on the sheet:
  //   Attention, votre version de Logisim
  //   ne contient pas de tracker. Si vous
  //   enregistrez votre projet, toutes les
  //   informations du tracker seront
  //   définitivement effacées.
endmodule
